// Logisim project MIPS.circ as structural Verilog: 7 circuits, main circuit main
module main (
  input  Reset
);

  wire alu_1_zero, clk, control_1_alusrc, control_1_extop, control_1_memwrite, control_1_npc_sel,
       control_1_regdst, control_1_regwrite;
  wire [1:0] control_1_aluop, control_1_memtoreg;
  wire [4:0] multiplexer_1_out;
  wire [31:0] alu_1_c, dm_1_dmout, extender_1_b, ifu_1_instr, multiplexer_2_out, multiplexer_3_out,
       regfile_1_rd1, regfile_1_rd2;

  Clock u_Clk (.out(clk));
  IFU ifu_1 (.Reset(Reset), .IsBeq(control_1_npc_sel), .Zero(alu_1_zero), .Clk(clk), .Instr(ifu_1_instr));
  Control control_1 (
    .Memwrite(control_1_memwrite), .npc_sel(control_1_npc_sel), .extop(control_1_extop),
    .Aluop(control_1_aluop), .Regdst(control_1_regdst), .Alusrc(control_1_alusrc),
    .Memtoreg(control_1_memtoreg), .Regwrite(control_1_regwrite), .func(ifu_1_instr[5:0]),
    .op(ifu_1_instr[31:26]));
  Multiplexer #(.width(5)) multiplexer_1 (
    .in0(ifu_1_instr[20:16]), .in1(ifu_1_instr[15:11]), .out(multiplexer_1_out), .sel(control_1_regdst));
  RegFile regfile_1 (
    .Rd1(regfile_1_rd1), .Rd2(regfile_1_rd2), .A1(ifu_1_instr[25:21]), .A2(ifu_1_instr[20:16]),
    .A3(multiplexer_1_out), .Wd(multiplexer_3_out), .Clk(clk), .Reset(Reset), .Regwrite(control_1_regwrite));
  Extender extender_1 (.A(ifu_1_instr[15:0]), .Extop(control_1_extop), .B(extender_1_b));
  Multiplexer #(.width(32)) multiplexer_2 (
    .in0(regfile_1_rd2), .in1(extender_1_b), .out(multiplexer_2_out), .sel(control_1_alusrc));
  Multiplexer #(.select(2), .width(32)) multiplexer_3 (
    .in0(alu_1_c), .in1(dm_1_dmout), .in2(extender_1_b), .out(multiplexer_3_out), .sel(control_1_memtoreg));  // open: in3
  ALU alu_1 (.A(regfile_1_rd1), .B(multiplexer_2_out), .F(control_1_aluop), .C(alu_1_c), .Zero(alu_1_zero));
  DM dm_1 (
    .Reset(Reset), .Memwrite(control_1_memwrite), .A(alu_1_c[4:0]), .Memtoreg(control_1_memtoreg[0]),
    .Clk(clk), .D(regfile_1_rd2), .DMout(dm_1_dmout));
endmodule

module IFU (
  input  Reset,
  input  IsBeq,
  input  Zero,
  input  Clk,
  output [31:0] Instr
);

  wire and_1_out, not_1_out;
  wire [29:0] adder_1_out, bit_extender_1_out, multiplexer_1_out, multiplexer_2_out, register_1_q;

  and and_1 (and_1_out, IsBeq, not_1_out);
  not not_1 (not_1_out, Zero);
  Multiplexer #(.width(30)) multiplexer_1 (
    .in0(30'h1), .in1(bit_extender_1_out), .out(multiplexer_1_out), .sel(and_1_out));
  Adder #(.width(30)) adder_1 (.a(multiplexer_1_out), .b(register_1_q), .out(adder_1_out));  // open: cin, cout
  Register #(.width(30)) register_1 (.D(multiplexer_2_out), .en(1'b1), .clk(Clk), .Q(register_1_q));  // open: clr
  Multiplexer #(.width(30)) multiplexer_2 (.in0(adder_1_out), .in1({30{1'b0}}), .out(multiplexer_2_out), .sel(Reset));
  assign bit_extender_1_out = {{14{Instr[15]}}, Instr[15:0]};  // Bit_Extender bit_extender_1
  ROM #(.addrWidth(5), .dataWidth(32)) rom_1 (.addr(register_1_q[4:0]), .data(Instr));

  // Notes on the sheet:
  //   contents of rom_1 (hex, n*v repeats v):
  //   0 221821 412023 3c053f3f ac250000 8c260000 34440001 1083fff9
endmodule

module Extender (
  input  [15:0] A,
  input  Extop,
  output [31:0] B
);

  wire [31:0] bit_extender_1_out, shifter_1_out;

  assign bit_extender_1_out = {{16{A[15]}}, A};  // Bit_Extender bit_extender_1
  Shifter #(.width(32)) shifter_1 (.in(bit_extender_1_out), .\dist (5'b10000), .out(shifter_1_out));
  Multiplexer #(.width(32)) multiplexer_1 (.in0(bit_extender_1_out), .in1(shifter_1_out), .out(B), .sel(Extop));
endmodule

module Control (
  input  [5:0] func,
  input  [5:0] op,
  output [1:0] Memtoreg,
  output [1:0] Aluop,
  output Regdst,
  output Alusrc,
  output Regwrite,
  output Memwrite,
  output npc_sel,
  output extop
);

  wire add_out, not_1_out, not_2_out, not_3_out, not_4_out, not_5_out, not_6_out, not_7_out, not_8_out,
       not_9_out, not_10_out, not_11_out, not_12_out, ori_out, sub_out;

  not not_1 (not_1_out, func[5]);
  not not_2 (not_2_out, func[4]);
  not not_3 (not_3_out, func[3]);
  not not_4 (not_4_out, func[2]);
  not not_5 (not_5_out, func[1]);
  not not_6 (not_6_out, func[0]);
  not not_7 (not_7_out, op[5]);
  not not_8 (not_8_out, op[4]);
  not not_9 (not_9_out, op[3]);
  not not_10 (not_10_out, op[2]);
  not not_11 (not_11_out, op[1]);
  not not_12 (not_12_out, op[0]);
  and add (add_out, not_12_out, not_11_out, not_10_out, not_9_out, not_8_out, not_7_out, func[0], not_5_out, not_4_out, not_3_out, not_2_out, func[5]);
  and sub (sub_out, not_12_out, not_11_out, not_10_out, not_9_out, not_8_out, not_7_out, func[0], func[1], not_4_out, not_3_out, not_2_out, func[5]);
  and ori (ori_out, op[0], not_11_out, op[2], op[3], not_8_out, not_7_out);
  and lw (Memtoreg[0], op[0], op[1], not_10_out, not_9_out, not_8_out, op[5]);
  and sw (Memwrite, op[0], op[1], not_10_out, op[3], not_8_out, op[5]);
  and beq (npc_sel, not_12_out, not_11_out, op[2], not_9_out, not_8_out, not_7_out);
  and lui (extop, op[0], op[1], op[2], op[3], not_8_out, not_7_out);
  or or_1 (Regdst, add_out, sub_out);
  or or_2 (Alusrc, ori_out, Memtoreg[0], Memwrite);
  or or_3 (Regwrite, add_out, sub_out, extop, ori_out, Memtoreg[0]);
  or or_4 (Aluop[1], add_out, sub_out, Memtoreg[0], Memwrite, npc_sel);
  or or_5 (Aluop[0], add_out, ori_out, Memtoreg[0], Memwrite);

  assign Memtoreg[1] = extop;
endmodule

module RegFile (
  input  Regwrite,
  input  [4:0] A1,
  input  [4:0] A2,
  input  [4:0] A3,
  input  [31:0] Wd,
  input  Clk,
  input  Reset,
  output [31:0] Rd1,
  output [31:0] Rd2
);

  wire WE0, WE1, WE2, WE3, WE4, WE5, WE6, WE7, WE8, WE9, WE10, WE11, WE12, WE13, WE14, WE15, WE16, WE17,
       WE18, WE19, WE20, WE21, WE22, WE23, WE24, WE25, WE26, WE27, WE28, WE29, WE30, WE31;
  wire [31:0] Q0, Q1, Q2, Q3, Q4, Q5, Q6, Q7, Q8, Q9, Q10, Q11, Q12, Q13, Q14, Q15, Q16, Q17, Q18, Q19, Q20,
       Q21, Q22, Q23, Q24, Q25, Q26, Q27, Q28, Q29, Q30, Q31;

  Decoder #(.select(5)) decoder_1 (
    .out0(WE0), .out1(WE1), .out2(WE2), .out3(WE3), .out4(WE4), .out5(WE5), .out6(WE6), .out7(WE7),
    .out8(WE8), .out9(WE9), .out10(WE10), .out11(WE11), .out12(WE12), .out13(WE13), .out14(WE14),
    .out15(WE15), .out16(WE16), .out17(WE17), .out18(WE18), .out19(WE19), .out20(WE20), .out21(WE21),
    .out22(WE22), .out23(WE23), .out24(WE24), .out25(WE25), .out26(WE26), .out27(WE27), .out28(WE28),
    .out29(WE29), .out30(WE30), .out31(WE31), .sel(A3), .en(Regwrite));
  Register #(.width(32)) register_1 (.D(Wd), .en(WE0), .clk(Clk), .Q(Q0), .clr(Reset));
  Register #(.width(32)) register_2 (.D(Wd), .en(WE1), .clk(Clk), .Q(Q1), .clr(Reset));
  Register #(.width(32)) register_3 (.D(Wd), .en(WE2), .clk(Clk), .Q(Q2), .clr(Reset));
  Register #(.width(32)) register_4 (.D(Wd), .en(WE3), .clk(Clk), .Q(Q3), .clr(Reset));
  Register #(.width(32)) register_5 (.D(Wd), .en(WE4), .clk(Clk), .Q(Q4), .clr(Reset));
  Register #(.width(32)) register_6 (.D(Wd), .en(WE5), .clk(Clk), .Q(Q5), .clr(Reset));
  Register #(.width(32)) register_7 (.D(Wd), .en(WE6), .clk(Clk), .Q(Q6), .clr(Reset));
  Register #(.width(32)) register_8 (.D(Wd), .en(WE7), .clk(Clk), .Q(Q7), .clr(Reset));
  Register #(.width(32)) register_9 (.D(Wd), .en(WE8), .clk(Clk), .Q(Q8), .clr(Reset));
  Register #(.width(32)) register_10 (.D(Wd), .en(WE9), .clk(Clk), .Q(Q9), .clr(Reset));
  Register #(.width(32)) register_11 (.D(Wd), .en(WE10), .clk(Clk), .Q(Q10), .clr(Reset));
  Register #(.width(32)) register_12 (.D(Wd), .en(WE11), .clk(Clk), .Q(Q11), .clr(Reset));
  Register #(.width(32)) register_13 (.D(Wd), .en(WE12), .clk(Clk), .Q(Q12), .clr(Reset));
  Register #(.width(32)) register_14 (.D(Wd), .en(WE13), .clk(Clk), .Q(Q13), .clr(Reset));
  Register #(.width(32)) register_15 (.D(Wd), .en(WE14), .clk(Clk), .Q(Q14), .clr(Reset));
  Register #(.width(32)) register_16 (.D(Wd), .en(WE15), .clk(Clk), .Q(Q15), .clr(Reset));
  Register #(.width(32)) register_17 (.D(Wd), .en(WE16), .clk(Clk), .Q(Q16), .clr(Reset));
  Register #(.width(32)) register_18 (.D(Wd), .en(WE17), .clk(Clk), .Q(Q17), .clr(Reset));
  Register #(.width(32)) register_19 (.D(Wd), .en(WE18), .clk(Clk), .Q(Q18), .clr(Reset));
  Register #(.width(32)) register_20 (.D(Wd), .en(WE19), .clk(Clk), .Q(Q19), .clr(Reset));
  Register #(.width(32)) register_21 (.D(Wd), .en(WE20), .clk(Clk), .Q(Q20), .clr(Reset));
  Register #(.width(32)) register_22 (.D(Wd), .en(WE21), .clk(Clk), .Q(Q21), .clr(Reset));
  Register #(.width(32)) register_23 (.D(Wd), .en(WE22), .clk(Clk), .Q(Q22), .clr(Reset));
  Register #(.width(32)) register_24 (.D(Wd), .en(WE23), .clk(Clk), .Q(Q23), .clr(Reset));
  Register #(.width(32)) register_25 (.D(Wd), .en(WE24), .clk(Clk), .Q(Q24), .clr(Reset));
  Register #(.width(32)) register_26 (.D(Wd), .en(WE25), .clk(Clk), .Q(Q25), .clr(Reset));
  Register #(.width(32)) register_27 (.D(Wd), .en(WE26), .clk(Clk), .Q(Q26), .clr(Reset));
  Register #(.width(32)) register_28 (.D(Wd), .en(WE27), .clk(Clk), .Q(Q27), .clr(Reset));
  Register #(.width(32)) register_29 (.D(Wd), .en(WE28), .clk(Clk), .Q(Q28), .clr(Reset));
  Register #(.width(32)) register_30 (.D(Wd), .en(WE29), .clk(Clk), .Q(Q29), .clr(Reset));
  Register #(.width(32)) register_31 (.D(Wd), .en(WE30), .clk(Clk), .Q(Q30), .clr(Reset));
  Register #(.width(32)) register_32 (.D(Wd), .en(WE31), .clk(Clk), .Q(Q31), .clr(Reset));
  Multiplexer #(.select(5), .width(32)) multiplexer_1 (
    .in0(Q0), .in1(Q1), .in2(Q2), .in3(Q3), .in4(Q4), .in5(Q5), .in6(Q6), .in7(Q7), .in8(Q8), .in9(Q9),
    .in10(Q10), .in11(Q11), .in12(Q12), .in13(Q13), .in14(Q14), .in15(Q15), .in16(Q16), .in17(Q17),
    .in18(Q18), .in19(Q19), .in20(Q20), .in21(Q21), .in22(Q22), .in23(Q23), .in24(Q24), .in25(Q25),
    .in26(Q26), .in27(Q27), .in28(Q28), .in29(Q29), .in30(Q30), .in31(Q31), .out(Rd1), .sel(A1));
  Multiplexer #(.select(5), .width(32)) multiplexer_2 (
    .in0(Q0), .in1(Q1), .in2(Q2), .in3(Q3), .in4(Q4), .in5(Q5), .in6(Q6), .in7(Q7), .in8(Q8), .in9(Q9),
    .in10(Q10), .in11(Q11), .in12(Q12), .in13(Q13), .in14(Q14), .in15(Q15), .in16(Q16), .in17(Q17),
    .in18(Q18), .in19(Q19), .in20(Q20), .in21(Q21), .in22(Q22), .in23(Q23), .in24(Q24), .in25(Q25),
    .in26(Q26), .in27(Q27), .in28(Q28), .in29(Q29), .in30(Q30), .in31(Q31), .out(Rd2), .sel(A2));

  // Other names for the same wires on the sheet: write[31:0] = Wd
endmodule

module ALU (
  input  [31:0] A,
  input  [31:0] B,
  input  [1:0] F,
  output [31:0] C,
  output Zero
);

  wire [31:0] adder_1_out, or_1_out, subtractor_1_out;

  Subtractor #(.width(32)) subtractor_1 (.a(A), .b(B), .out(subtractor_1_out));  // open: bin, bout
  Adder #(.width(32)) adder_1 (.a(A), .b(B), .out(adder_1_out));  // open: cin, cout
  assign or_1_out = B | A;  // OR_Gate or_1, 32 bits wide
  Multiplexer #(.select(2), .width(32)) multiplexer_1 (
    .in0({32{1'b0}}), .in1(or_1_out), .in2(subtractor_1_out), .in3(adder_1_out), .out(C), .sel(F));
  or or_2 (Zero, C[0], C[1], C[2], C[3], C[4], C[5], C[6], C[7], C[8], C[9], C[10], C[11], C[12], C[13], C[14], C[15], C[16], C[17], C[18], C[19], C[20], C[21], C[22], C[23], C[24], C[25], C[26], C[27], C[28], C[29], C[30], C[31]);
endmodule

module DM (
  input  Reset,
  input  Memwrite,
  input  [4:0] A,
  input  Memtoreg,
  input  Clk,
  input  [31:0] D,
  output [31:0] DMout
);

  RAM #(.addrWidth(5), .asyncread("true"), .clearpin("true"), .dataWidth(32)) ram_1 (
    .addr(A), .we(Memwrite), .oe(Memtoreg), .clk(Clk), .din(D), .dout(DMout), .clr(Reset));
endmodule
